# Fritzing sketch Scraps 2 Circuit Diagram (saved by Fritzing 0.9.10b)
breadboards: 1

parts:
  OLED1 = 128x32 I2C Monochrome OLED Display
  Part1 = Arduino Uno (Rev3)
  S1 = Pushbutton [package="[THT]"]
  S2 = Pushbutton [package="[THT]"]
  S3 = Pushbutton [package="[THT]"]
  S4 = Pushbutton [package="[THT]"]
  R1 = Resistor [tolerance=±5% power=0.25 resistance=220 package=THT]
  R2 = Resistor [tolerance=±5% power=0.25 resistance=220 package=THT]
  R3 = Resistor [tolerance=±5% power=0.25 resistance=220 package=THT]
  R4 = Resistor [tolerance=±5% power=0.25 resistance=220 package=THT]
  Q1 = MOSFET-NCHANNEL [package=to220v]
  R5 = Resistor [tolerance=±5% power=0.25 resistance=220 package=THT]
  J1 = Piezo Speaker
  R6 = Heating Pad

nets:
  N1: OLED1.SDA, Part1.A5/SCL
  N2: Part1.D8, J1.pin2
  N3: Part1.GND, R1.Pin_1, R2.Pin_1, R3.Pin_1, R4.Pin_1, Q1.S, R5.Pin_1, J1.pin1
  N4: Part1.D3_PWM, S4.Pin_1, S4.Pin_2, R4.Pin_0
  N5: Part1.D4, S3.Pin_1, S3.Pin_2, R3.Pin_0
  N6: Part1.D5_PWM, S2.Pin_1, R2.Pin_0
  N7: Part1.D6_PWM, S1.Pin_1, S1.Pin_2, R1.Pin_0
  N8: Part1.D7, Q1.G, R5.Pin_0
  N9: Part1.5V, S1.Pin_3, S1.Pin_4, S2.Pin_3, S2.Pin_4, S3.Pin_3, S3.Pin_4, S4.Pin_3, S4.Pin_4
  N10: Part1.VIN, R6.pin_1
  N11: Q1.D, R6.pin_0

notes:
  connected by Qwiic cable

custom parts:
  Heating Pad: A thermoresistant material with an embeded conductor that dissipates electrical energy into heat.

// code stored in the sketch: Scraps 2 Circuit Diagram.ino
#include <SPI.h>
#include <Wire.h>
#include <Adafruit_GFX.h>
#include <Adafruit_SSD1306.h>

#define resetButton 6
#define lowButton 5
#define medButton 4
#define highButton 3
#define mosfetGate 7
#define buzzer 8

int outputLevel = 0; //heat to mosfetGate
int heatState = 0; //state of system, keeps track of what year to display
int heatLevel = 0;
double holdMillis = 0;

#define OLED_RESET 4
Adafruit_SSD1306 display(OLED_RESET);

void setup() {
  Serial.begin(9600);
  display.begin(SSD1306_SWITCHCAPVCC, 0x3C);  // initialize with the I2C addr 0x3C (for the 128x32)
  // init done
  display.clearDisplay();
  delay(1000);
  pinMode(resetButton, INPUT);
  pinMode(lowButton, INPUT);
  pinMode(medButton, INPUT);
  pinMode(highButton, INPUT);
  pinMode(mosfetGate, OUTPUT);
  display.clearDisplay();
}

void loop() {

    switch(heatState) {
    case 0:
      outputLevel = 0;
      analogWrite(mosfetGate, outputLevel);
      tone(buzzer, 131);
      resetScrollText();
      delay(50);
      display.clearDisplay();
      delay(50);
      break;
    case 1:
      outputLevel = 70;
      analogWrite(mosfetGate, outputLevel);
      tone(buzzer, 82);
      lowScrollText();
      delay(50);
      display.clearDisplay();
      delay(50);
      break;
    case 2:
      outputLevel = 170;
      analogWrite(mosfetGate, outputLevel);
      tone(buzzer, 20);
      medScrollText();
      delay(50);
      display.clearDisplay();
      delay(50);
      break;
    case 3:
      outputLevel = 255;
      analogWrite(mosfetGate, outputLevel);
      tone(buzzer, 39);
      highScrollText();
      delay(50);
      display.clearDisplay();
      delay(50);
      break;
}

  if (digitalRead(resetButton) == HIGH) {
    heatState = 0;
  }
   if (digitalRead(lowButton) == HIGH) {
    heatState = 1;
  } 
  if (digitalRead(medButton) == HIGH) {
    heatState = 2;
  }
   if (digitalRead(highButton) == HIGH) {
    heatState = 3;
  }

}

void highScrollText(void) {
  holdMillis = millis();
  display.setTextSize(4);
  display.setTextColor(WHITE);
  display.setCursor(20,2);
  display.clearDisplay();
  display.println("2018");
  display.display();
  delay(3000);
  display.setTextSize(2);
  display.setTextColor(WHITE);
  display.setCursor(1,0);
  display.clearDisplay();
  display.print("11,300,000   tons");
  display.display();
  delay(500);
  
  while ((digitalRead(resetButton) == LOW) && (digitalRead(lowButton) == LOW) && (digitalRead(medButton) == LOW) && ((millis() - holdMillis) < 17000) ) {
    //Scroll text to the left
    display.startscrollleft(0x00, 0x0F);
  }

if (digitalRead(resetButton) == HIGH) {
    heatState = 0;
}
if (digitalRead(lowButton) == HIGH) {
    heatState = 1;
}
if (digitalRead(medButton) == HIGH) {
    heatState = 2;
}
 
  holdMillis = millis();
  display.stopscroll();
}

void medScrollText(void) {
  holdMillis = millis();
  display.setTextSize(4);
  display.setTextColor(WHITE);
  display.setCursor(20,2);
  display.clearDisplay();
  display.println("2000");
  display.display();
  delay(3000);
  display.setTextSize(2);
  display.setTextColor(WHITE);
  display.setCursor(15,0);
  display.clearDisplay();
  display.print("6,280,000    tons");
  display.display();
  delay(500);
  
  while ((digitalRead(resetButton) == LOW) && (digitalRead(lowButton) == LOW) && (digitalRead(highButton) == LOW) && ((millis() - holdMillis) < 17000) ) {
    //Scroll text to the left
    display.startscrollleft(0x00, 0x0F);
  }

if (digitalRead(resetButton) == HIGH) {
    heatState = 0;
}
if (digitalRead(lowButton) == HIGH) {
    heatState = 1;
}
if (digitalRead(highButton) == HIGH) {
    heatState = 3;
}
 
  holdMillis = millis();
  display.stopscroll();
}

void lowScrollText(void) {
  holdMillis = millis();
  display.setTextSize(4);
  display.setTextColor(WHITE);
  display.setCursor(20,2);
  display.clearDisplay();
  display.println("1980");
  display.display();
  delay(3000);
  display.setTextSize(2);
  display.setTextColor(WHITE);
  display.setCursor(15,0);
  display.clearDisplay();
  display.print("2,320,000    tons");
  display.display();
  delay(500);
  
  while ((digitalRead(resetButton) == LOW) && (digitalRead(highButton) == LOW) && (digitalRead(medButton) == LOW) && ((millis() - holdMillis) < 17000) ) {
    //Scroll text to the left
    display.startscrollleft(0x00, 0x0F);
  }

if (digitalRead(resetButton) == HIGH) {
    heatState = 0;
}
if (digitalRead(highButton) == HIGH) {
    heatState = 3;
}
if (digitalRead(medButton) == HIGH) {
    heatState = 2;
}
 
  holdMillis = millis();
  display.stopscroll();
}

void resetScrollText(void) {
  holdMillis = millis();
  display.setTextSize(4);
  display.setTextColor(WHITE);
  display.setCursor(20,2);
  display.clearDisplay();
  display.println("1960");
  display.display();
  delay(3000);
  display.setTextSize(2);
  display.setTextColor(WHITE);
  display.setCursor(15,0);
  display.clearDisplay();
  display.print("1,710,000    tons");
  display.display();
  delay(500);
  
  while ((digitalRead(highButton) == LOW) && (digitalRead(lowButton) == LOW) && (digitalRead(medButton) == LOW) && ((millis() - holdMillis) < 17000) ) {
    //Scroll text to the left
    display.startscrollleft(0x00, 0x0F);
  }

if (digitalRead(highButton) == HIGH) {
    heatState = 3;
}
if (digitalRead(lowButton) == HIGH) {
    heatState = 1;
}
if (digitalRead(medButton) == HIGH) {
    heatState = 2;
}
 
  holdMillis = millis();
  display.stopscroll();
}
